# Fritzing sketch servo (saved by Fritzing 0.8.7b)
breadboards: 1

parts:
  Part1 = Arduino Uno (Rev3)
  R1 = Rotary Potentiometer (Small) [maximum_resistance=100kΩ package=THT]
  J1 = Basic Servo

nets:
  N1: Part1.A1, R1.wiper
  N2: Part1.D9_PWM, J1.pulse
  5V: Part1.5V, R1.leg2, J1.vcc
  GND: Part1.GND, R1.leg1, J1.gnd
