# Fritzing sketch speaker (saved by Fritzing 0.8.7b)
breadboards: 1

parts:
  Part1 = Arduino Uno (Rev3)
  R1 = Rotary Potentiometer (Small) [maximum_resistance=100kΩ package=THT]
  J1 = Piezo Speaker

nets:
  N1: Part1.A1, R1.wiper
  N2: Part1.D11_PWM/MOSI, J1.pin2
  N3: Part1.5V, R1.leg2
  N4: Part1.GND, R1.leg1, J1.pin1
