# Fritzing sketch blink (saved by Fritzing 0.8.7b)
breadboards: 1

parts:
  Part1 = Arduino Uno (Rev3)
  LED1 = LED - 5mm [color="Red (633nm)" package="5 mm [THT]"]
  R1 = Rotary Potentiometer (Small) [maximum_resistance=100kΩ package=THT]

nets:
  N1: Part1.A1, R1.wiper
  N2: Part1.D12/MISO, LED1.anode
  N3: Part1.5V, R1.leg2
  N4: Part1.GND, LED1.cathode, R1.leg1
