# Fritzing sketch solenoid (saved by Fritzing 0.8.7b)
breadboards: 1

parts:
  Part1 = Arduino Uno (Rev3)
  R1 = Rotary Potentiometer (Small) [maximum_resistance=100kΩ package=THT]
  L1 = Solenoid
  Q1 = npn-Powertransistor [package="TO220 [THT]"]
  D1 = Rectifier Diode [part_number=1N4001 package="300 mil [THT]"]  # not connected

nets:
  N1: Part1.A1, R1.wiper
  N2: Part1.D12/MISO, Q1.base
  N3: Part1.5V, R1.leg2, L1.pin2
  N4: Part1.GND, R1.leg1, Q1.emitter
  N5: L1.pin1, Q1.collector
