# Fritzing sketch steps (saved by Fritzing 0.8.7b)
breadboards: 1

parts:
  Part1 = Arduino Uno (Rev3)
  LED1 = LED - 5mm [color="Red (633nm)" package="5 mm [THT]"]
  R1 = Rotary Potentiometer (Small) [maximum_resistance=100kΩ package=THT]
  LED2 = LED - 5mm [color="Red (633nm)" package="5 mm [THT]"]
  LED3 = LED - 5mm [color="Red (633nm)" package="5 mm [THT]"]
  LED4 = LED - 5mm [color="Red (633nm)" package="5 mm [THT]"]
  LED5 = LED - 5mm [color="Red (633nm)" package="5 mm [THT]"]

nets:
  N1: Part1.A1, R1.wiper
  N2: Part1.GND, LED1.cathode, R1.leg1, LED2.cathode, LED3.cathode, LED4.cathode, LED5.cathode
  N3: Part1.D2, LED1.anode
  N4: Part1.D3_PWM, LED2.anode
  N5: Part1.D4, LED3.anode
  N6: Part1.D5_PWM, LED4.anode
  N7: Part1.D6_PWM, LED5.anode
  N8: Part1.5V, R1.leg2
